// Logisim project Es1.circ as structural Verilog: 1 circuit, main circuit main
module main (
  input  A,
  input  B,
  input  C
);

  wire and_1_out, and_2_out, and_3_out, nor_1_out, or_1_out, OUT_out;

  or or_1 (or_1_out, B, C);
  nor nor_1 (nor_1_out, B, C);
  and and_1 (and_1_out, A, or_1_out);
  and and_2 (and_2_out, A, B, C);
  and and_3 (and_3_out, C, nor_1_out);
  LED led_1 (.in(OUT_out));
  or OUT (OUT_out, and_1_out, and_3_out, and_2_out);
endmodule
