// Logisim project Es2.circ as structural Verilog: 1 circuit, main circuit main
module main (
  input  A,
  input  B,
  input  C
);

  wire and_1_out, and_2_out, and_3_out, or_1_out;

  and and_1 (and_1_out, A, B);
  and and_2 (and_2_out, A, C);
  and and_3 (and_3_out, and_2_out, B);
  or or_1 (or_1_out, and_1_out, and_2_out);
  LED X (.in(or_1_out));
  LED Y (.in(and_3_out));
endmodule
