// Logisim project Es3.circ as structural Verilog: 1 circuit, main circuit main
module main (
  input  A,
  input  B,
  input  C,
  input  D
);

  wire _1_out, _2_out, _3_out, not_1_out, not_2_out, not_3_out, or_1_out;

  not not_1 (not_1_out, A);
  not not_2 (not_2_out, B);
  not not_3 (not_3_out, C);
  // NOT_Gate not_4 has open pins: in=D, out=open
  and _1 (_1_out, C, B, not_1_out);
  and _2 (_2_out, not_3_out, A, D);
  and _3 (_3_out, A, not_2_out, D);
  or or_1 (or_1_out, _1_out, _2_out, _3_out);
  LED X (.in(or_1_out));
endmodule
