// Logisim project Es4.circ as structural Verilog: 1 circuit, main circuit main
module main (
);

  wire CLR_out, INC_out, multiplexer_1_out, multiplexer_2_out, multiplexer_3_out, multiplexer_4_out,
       multiplexer_5_out, multiplexer_6_out, multiplexer_7_out;
  wire [1:0] CTR_q;

  Multiplexer #(.select(2), .disabled(0)) multiplexer_1 (
    .in0(1'b1), .in2(1'b1), .in3(1'b1), .out(multiplexer_1_out), .sel(CTR_q), .en(1'b1));  // open: in1
  Multiplexer #(.select(2), .disabled(0)) multiplexer_2 (
    .in0(1'b1), .in1(1'b1), .in2(1'b1), .in3(1'b1), .out(multiplexer_2_out), .sel(CTR_q), .en(1'b1));
  Multiplexer #(.select(2), .disabled(0)) multiplexer_3 (
    .in0(1'b1), .in1(1'b1), .in3(1'b1), .out(multiplexer_3_out), .sel(CTR_q), .en(1'b1));  // open: in2
  Multiplexer #(.select(2), .disabled(0)) multiplexer_4 (
    .in0(1'b1), .in2(1'b1), .in3(1'b1), .out(multiplexer_4_out), .sel(CTR_q), .en(1'b1));  // open: in1
  Multiplexer #(.select(2), .disabled(0)) multiplexer_5 (
    .in0(1'b1), .in2(1'b1), .out(multiplexer_5_out), .sel(CTR_q), .en(1'b1));  // open: in1, in3
  Multiplexer #(.select(2), .disabled(0)) multiplexer_6 (
    .in0(1'b1), .out(multiplexer_6_out), .sel(CTR_q), .en(1'b1));  // open: in1, in2, in3
  Multiplexer #(.select(2), .disabled(0)) multiplexer_7 (
    .in2(1'b1), .in3(1'b1), .out(multiplexer_7_out), .sel(CTR_q), .en(1'b1));  // open: in0, in1
  Counter #(.width(2), .max('h3)) CTR (.load(1'b0), .Q(CTR_q), .clk(INC_out), .clr(CLR_out));  // open: D, count, carry
  Button INC (.out(INC_out));
  Button CLR (.out(CLR_out));
  _7_Segment_Display u_7_segment_display_1 (
    .g(multiplexer_7_out), .f(multiplexer_6_out), .a(multiplexer_1_out), .b(multiplexer_2_out),
    .e(multiplexer_5_out), .d(multiplexer_4_out), .c(multiplexer_3_out));  // open: dp
endmodule
