// Logisim project Es2.circ as structural Verilog: 1 circuit, main circuit main
module main (
  input  S,
  input  R,
  output out_3,
  output out_4
);

  wire nand_1_out, nand_2_out, nand_3_out, nand_4_out, nand_5_out, nand_6_out;

  nand nand_1 (nand_1_out, S, S);
  nand nand_2 (nand_2_out, out_4, out_4);
  nand nand_3 (nand_3_out, R, R);
  nand nand_4 (nand_4_out, out_3, out_3);
  nand nand_5 (nand_5_out, nand_1_out, nand_2_out);
  nand nand_6 (nand_6_out, nand_3_out, nand_4_out);
  nand nand_7 (out_3, nand_5_out, nand_5_out);
  nand nand_8 (out_4, nand_6_out, nand_6_out);
endmodule
