// Logisim project Es3 (SR + Sync).circ as structural Verilog: 1 circuit, main circuit main
module main (
  input  in_1,
  input  in_2,
  output out_3,
  output out_4
);

  wire and_1_out, and_2_out, CLK_out;

  Clock #(.highDuration(2)) CLK (.out(CLK_out));
  and and_1 (and_1_out, in_1, CLK_out);
  and and_2 (and_2_out, in_2, CLK_out);
  nor nor_1 (out_3, and_1_out, out_4);
  nor nor_2 (out_4, and_2_out, out_3);
endmodule
