// Logisim project Es4 (Latch D).circ as structural Verilog: 1 circuit, main circuit main
module main (
  input  D,
  output out_2,
  output out_3
);

  wire and_1_out, and_2_out, not_1_out;

  not not_1 (not_1_out, D);
  and and_1 (and_1_out, 1'b1, not_1_out);
  and and_2 (and_2_out, 1'b1, D);
  nor nor_1 (out_2, and_1_out, out_3);
  nor nor_2 (out_3, and_2_out, out_2);
endmodule
