// Logisim project Es5 (FF JK).circ as structural Verilog: 1 circuit, main circuit main
module main (
  input  in_1,
  input  in_2,
  output out_3,
  output out_4
);

  wire CLK_out, nand_1_out, nand_2_out, nand_3_out, nand_4_out, nand_5_out, nand_6_out, not_1_out;

  Clock #(.highDuration(2)) CLK (.out(CLK_out));
  nand nand_1 (nand_1_out, in_1, CLK_out);
  nand nand_2 (nand_2_out, in_2, CLK_out);
  nand nand_3 (nand_3_out, nand_1_out, nand_4_out);
  nand nand_4 (nand_4_out, nand_2_out, nand_3_out);
  not not_1 (not_1_out, CLK_out);
  nand nand_5 (nand_5_out, nand_3_out, not_1_out);
  nand nand_6 (nand_6_out, nand_4_out, not_1_out);
  nand nand_7 (out_3, nand_5_out, out_4);
  nand nand_8 (out_4, nand_6_out, out_3);
endmodule
