// Logisim project FSM_Counter_Mod4.circ as structural Verilog: 1 circuit, main circuit main
module main (
  input  EN,
  output out_2,
  output COUNTER_DISPLAY
);

  wire and_1_out, and_2_out, CLK_out, decoder_1_out0, decoder_1_out1, decoder_1_out2, decoder_1_out3,
       or_1_out, or_2_out;

  Clock CLK (.out(CLK_out));
  and and_1 (and_1_out, or_2_out, EN);
  and and_2 (and_2_out, or_1_out, EN);
  D_Flip_Flop d_ff_1 (.clk(CLK_out), .D(and_1_out), .Q(out_2));  // open: Qn, preset, en, reset
  D_Flip_Flop d_ff_2 (.clk(CLK_out), .D(and_2_out), .Q(COUNTER_DISPLAY));  // open: Qn, preset, en, reset
  Decoder #(.select(2), .enable("false")) decoder_1 (
    .out0(decoder_1_out0), .out1(decoder_1_out1), .out2(decoder_1_out2), .out3(decoder_1_out3),
    .sel({out_2, COUNTER_DISPLAY}));
  or or_1 (or_1_out, 1'b0, decoder_1_out2, 1'b0, decoder_1_out0);
  or or_2 (or_2_out, 1'b0, decoder_1_out2, decoder_1_out1, 1'b0);
endmodule
